# Fritzing sketch robocop (saved by Fritzing 0.8.3b)
breadboards: 1

parts:
  J1 = Basic Force Sensing Resistor (FSR) [package=THT]
  J2 = Basic Force Sensing Resistor (FSR) [package=THT]
  R1 = Resistor [tolerance=±5% resistance=220 package=THT]
  R2 = Resistor [tolerance=±5% resistance=220 package=THT]
  Part1 = Arduino Uno (Rev3)
  J3 = Basic Servo
  J4 = Basic Servo

nets:
  VCC: J1.pin_0, J2.pin_1, Part1.5V, J3.vcc, J4.vcc
  N1: J1.pin_1, R2.Pin_1, Part1.A0
  N2: J2.pin_0, R1.Pin_1, Part1.A1
  GND: R1.Pin_0, R2.Pin_0, Part1.GND, J3.gnd, J4.gnd
  N3: Part1.D1/TX, J4.pulse
  N4: Part1.D2, J3.pulse
